// Logisim project CPU.circ as structural Verilog: 5 circuits, main circuit main
module main (
  input  in_1,
  input  in_2,
  input  in_3,
  input  in_4,
  input  in_5,
  input  in_6,
  input  in_7,
  input  in_8,
  input  in_9,
  input  in_10,
  input  in_11,
  input  in_12,
  input  in_13,
  input  in_14,
  input  in_15,
  input  in_16,
  input  in_17,
  input  in_18,
  input  in_19,
  input  in_20,
  input  in_21,
  input  in_22,
  input  in_23,
  input  in_24,
  input  in_25,
  input  in_26,
  input  in_27,
  input  in_28,
  input  in_29,
  input  in_30,
  input  in_31,
  input  in_32,
  input  in_33,
  input  in_34,
  input  in_35,
  input  in_36
);

  wire and_1_out, and_2_out, Clk, Clk_t, clock_1_out, DI_nCntEna, Hadda_nOE, hm62256sel_1_load,
       hm62256sel_1_sel, Ladda_nOE, MAR_nCntEna, MEM_ne, MEM_ns, PC_nCntEna, RA_nCntEna, RAz, RB_nCntEna,
       RBz, RC_nCntEna, RCz, RD_nCntEna, RDz, SI_nCntEna, SP_nCntEna;
  wire [7:0] n8bitreg_1_dout, n8bitreg_1_dout_2, n8bitreg_2_dout, n8bitreg_3_dout, n8bitreg_3_dout_2,
       n8bitreg_4_dout, n8bitreg_5_dout, n8bitreg_6_dout, n16bitreg_1_dout_2;
  wire [15:0] n16bitreg_1_dout, n16bitreg_2_dout, n16bitreg_3_dout, n16bitreg_4_dout, n16bitreg_5_dout,
       n16bitreg_5_dout_2;

  Clock clock_1 (.out(clock_1_out));
  not not_1 (SP_nCntEna, in_4);
  not not_2 (PC_nCntEna, in_7);
  not not_3 (DI_nCntEna, in_10);
  not not_4 (SI_nCntEna, in_13);
  not not_5 (MAR_nCntEna, in_16);
  not not_6 (Hadda_nOE, in_21);
  not not_7 (Ladda_nOE, in_22);
  not not_8 (RA_nCntEna, in_23);
  not not_9 (RB_nCntEna, in_26);
  not not_10 (RC_nCntEna, in_29);
  not not_11 (RD_nCntEna, in_32);
  not not_12 (MEM_ne, in_35);
  not not_13 (MEM_ns, in_36);
  buf buffer_1 (Clk, clock_1_out);
  not not_14 (Clk_t, clock_1_out);
  _8bitreg u_8bitreg_1 (
    .Load(in_18), .Clock(Clk), .DataIn(n8bitreg_3_dout_2), .nCntEna(1'b1), .Reset(in_1), .Up_nDown(1'b0),
    .Enable(in_19), .Dout(n8bitreg_1_dout), .Dout_2(n8bitreg_1_dout_2));  // open: Zout
  _8bitreg u_8bitreg_2 (
    .Load(in_2), .Clock(Clk), .DataIn(n8bitreg_3_dout_2), .nCntEna(1'b1), .Reset(in_1), .Up_nDown(1'b0),
    .Enable(1'b1), .Dout(n8bitreg_2_dout));  // open: Dout_2, Zout
  // Probe on n8bitreg_2_dout
  // Probe on n8bitreg_1_dout
  _16bitreg u_16bitreg_1 (
    .DataIn({n16bitreg_1_dout_2, n8bitreg_1_dout_2}), .Clock(Clk_t), .Load(in_5), .nCntEna(SP_nCntEna),
    .Up_nDown(in_3), .Reset(in_1), .Enable(in_6), .Dout(n16bitreg_1_dout),
    .Dout_2({n16bitreg_1_dout_2, n8bitreg_1_dout_2}));
  // Probe on n16bitreg_1_dout
  _16bitreg u_16bitreg_2 (
    .DataIn({n16bitreg_1_dout_2, n8bitreg_1_dout_2}), .Clock(Clk_t), .Load(in_8), .nCntEna(PC_nCntEna),
    .Up_nDown(in_3), .Reset(in_1), .Enable(in_9), .Dout(n16bitreg_2_dout),
    .Dout_2({n16bitreg_1_dout_2, n8bitreg_1_dout_2}));
  // Probe on n16bitreg_2_dout
  _8bitreg u_8bitreg_3 (
    .Load(in_24), .Clock(Clk_t), .DataIn(n8bitreg_3_dout_2), .nCntEna(RA_nCntEna), .Reset(in_1),
    .Up_nDown(in_3), .Enable(in_25), .Dout(n8bitreg_3_dout), .Dout_2(n8bitreg_3_dout_2), .Zout(RAz));
  // Probe on n8bitreg_3_dout
  _8bitreg u_8bitreg_4 (
    .Load(in_27), .Clock(Clk_t), .DataIn(n8bitreg_3_dout_2), .nCntEna(RB_nCntEna), .Reset(in_1),
    .Up_nDown(in_3), .Enable(in_28), .Dout(n8bitreg_4_dout), .Dout_2(n8bitreg_3_dout_2), .Zout(RBz));
  _16bitreg u_16bitreg_3 (
    .DataIn({n16bitreg_1_dout_2, n8bitreg_1_dout_2}), .Clock(Clk_t), .Load(in_11), .nCntEna(DI_nCntEna),
    .Up_nDown(in_3), .Reset(in_1), .Enable(in_12), .Dout(n16bitreg_3_dout),
    .Dout_2({n16bitreg_1_dout_2, n8bitreg_1_dout_2}));
  // Probe on n16bitreg_3_dout
  // Probe on n8bitreg_4_dout
  _16bitreg u_16bitreg_4 (
    .DataIn({n16bitreg_1_dout_2, n8bitreg_1_dout_2}), .Clock(Clk_t), .Load(in_14), .nCntEna(SI_nCntEna),
    .Up_nDown(in_3), .Reset(in_1), .Enable(in_15), .Dout(n16bitreg_4_dout),
    .Dout_2({n16bitreg_1_dout_2, n8bitreg_1_dout_2}));
  _8bitreg u_8bitreg_5 (
    .Load(in_30), .Clock(Clk_t), .DataIn(n8bitreg_3_dout_2), .nCntEna(RC_nCntEna), .Reset(in_1),
    .Up_nDown(in_3), .Enable(in_31), .Dout(n8bitreg_5_dout), .Dout_2(n8bitreg_3_dout_2), .Zout(RCz));
  // Probe on n8bitreg_5_dout
  // Probe on n16bitreg_4_dout
  and and_1 (and_1_out, in_20, ~Hadda_nOE);  // AND_Gate
  assign n8bitreg_3_dout_2 = and_1_out ? n16bitreg_1_dout_2 : 8'bz;  // Controlled_Buffer controlled_buffer_1
  assign n16bitreg_1_dout_2 = and_2_out ? n8bitreg_3_dout_2 : 8'bz;  // Controlled_Buffer controlled_buffer_2
  assign n8bitreg_3_dout_2 = Ladda_nOE ? n8bitreg_1_dout_2 : 8'bz;  // Controlled_Buffer controlled_buffer_3
  _8bitreg u_8bitreg_6 (
    .Load(in_33), .Clock(Clk_t), .DataIn(n8bitreg_3_dout_2), .nCntEna(RD_nCntEna), .Reset(in_1),
    .Up_nDown(in_3), .Enable(in_34), .Dout(n8bitreg_6_dout), .Dout_2(n8bitreg_3_dout_2), .Zout(RDz));
  // Probe on n8bitreg_6_dout
  and and_2 (and_2_out, ~in_20, ~Hadda_nOE);  // AND_Gate
  // Probe on n16bitreg_5_dout
  _16bitreg u_16bitreg_5 (
    .DataIn({n16bitreg_1_dout_2, n8bitreg_1_dout_2}), .Clock(Clk_t), .Load(in_17), .nCntEna(MAR_nCntEna),
    .Up_nDown(in_3), .Reset(in_1), .Enable(1'b1), .Dout(n16bitreg_5_dout), .Dout_2(n16bitreg_5_dout_2));
  HM62256sel hm62256sel_1 (.nWE(MEM_ns), .nCE(1'b0), .nOE(MEM_ne), .Sel(hm62256sel_1_sel), .Load(hm62256sel_1_load));
  RAM #(.addrWidth(16), .bus("asynch")) ram_1 (
    .addr(n16bitreg_5_dout_2), .data(n8bitreg_3_dout_2), .sel(hm62256sel_1_sel), .ld(hm62256sel_1_load));  // open: clr

  // Other names for the same wires on the sheet: DIena = in_12; DIload = in_11; Had_nda = in_20; IRload = in_2;
  //   lTMPena = in_19; lTMPload = in_18; MARload = in_17; PCena = in_9; PCload = in_8; RAena = in_25; RAload = in_24;
  //   RBena = in_28; RBload = in_27; RCena = in_31; RCload = in_30; RDena = in_34; RDload = in_33; Rst = in_1;
  //   SIena = in_15; SIload = in_14; SPena = in_6; SPload = in_5; U_nD = in_3

  // Notes on the sheet:
  //   lTMP
  //   IR
  //   SP
  //   PC
  //   RA
  //   RB
  //   DI
  //   RC
  //   SI
  //   RD
  //   MAR
endmodule

module _8bitreg (
  input  Load,
  input  Clock,
  input  [7:0] DataIn,
  input  nCntEna,
  input  Reset,
  input  Up_nDown,
  input  Enable,
  output Zout,
  output [7:0] Dout,
  output [7:0] Dout_2
);

  wire cd4516be_1_ncarryout;

  CD4516BE cd4516be_1 (
    .P0(DataIn[0]), .P1(DataIn[1]), .P2(DataIn[2]), .P3(DataIn[3]), .Reset(Reset), .Preset_Enable(Load),
    .Clock(Clock), .nCarryOut(cd4516be_1_ncarryout), .nCarryIn(nCntEna), .Up_Down(Up_nDown), .Q0(Dout[0]),
    .Q1(Dout[1]), .Q2(Dout[2]), .Q3(Dout[3]));  // open: VCC, VSS
  CD4516BE cd4516be_2 (
    .P0(DataIn[4]), .P1(DataIn[5]), .P2(DataIn[6]), .P3(DataIn[7]), .Reset(Reset), .Preset_Enable(Load),
    .Clock(Clock), .nCarryIn(cd4516be_1_ncarryout), .Up_Down(Up_nDown), .Q0(Dout[4]), .Q1(Dout[5]),
    .Q2(Dout[6]), .Q3(Dout[7]));  // open: nCarryOut, VCC, VSS
  nor nor_1 (Zout, Dout[7], Dout[6], Dout[5], Dout[4], Dout[3], Dout[2], Dout[1], Dout[0]);
  assign Dout_2 = Enable ? Dout : 8'bz;  // Controlled_Buffer controlled_buffer_1

  // Notes on the sheet:
  //   Dout_2: pull=down
  //   74HC4078
endmodule

module _16bitreg (
  input  [15:0] DataIn,
  input  Load,
  input  Clock,
  input  nCntEna,
  input  Up_nDown,
  input  Reset,
  input  Enable,
  output [15:0] Dout,
  output [15:0] Dout_2
);

  wire cd4516be_1_ncarryout, cd4516be_2_ncarryout, cd4516be_3_ncarryout;

  CD4516BE cd4516be_1 (
    .P0(DataIn[0]), .P1(DataIn[1]), .P2(DataIn[2]), .P3(DataIn[3]), .Reset(Reset), .Preset_Enable(Load),
    .Clock(Clock), .nCarryOut(cd4516be_1_ncarryout), .nCarryIn(nCntEna), .Up_Down(Up_nDown), .Q0(Dout[0]),
    .Q1(Dout[1]), .Q2(Dout[2]), .Q3(Dout[3]));  // open: VCC, VSS
  CD4516BE cd4516be_2 (
    .P0(DataIn[4]), .P1(DataIn[5]), .P2(DataIn[6]), .P3(DataIn[7]), .Reset(Reset), .Preset_Enable(Load),
    .Clock(Clock), .nCarryOut(cd4516be_2_ncarryout), .nCarryIn(cd4516be_1_ncarryout), .Up_Down(Up_nDown),
    .Q0(Dout[4]), .Q1(Dout[5]), .Q2(Dout[6]), .Q3(Dout[7]));  // open: VCC, VSS
  CD4516BE cd4516be_3 (
    .P0(DataIn[8]), .P1(DataIn[9]), .P2(DataIn[10]), .P3(DataIn[11]), .Reset(Reset), .Preset_Enable(Load),
    .Clock(Clock), .nCarryOut(cd4516be_3_ncarryout), .nCarryIn(cd4516be_2_ncarryout), .Up_Down(Up_nDown),
    .Q0(Dout[8]), .Q1(Dout[9]), .Q2(Dout[10]), .Q3(Dout[11]));  // open: VCC, VSS
  CD4516BE cd4516be_4 (
    .P0(DataIn[12]), .P1(DataIn[13]), .P2(DataIn[14]), .P3(DataIn[15]), .Reset(Reset), .Preset_Enable(Load),
    .Clock(Clock), .nCarryIn(cd4516be_3_ncarryout), .Up_Down(Up_nDown), .Q0(Dout[12]), .Q1(Dout[13]),
    .Q2(Dout[14]), .Q3(Dout[15]));  // open: nCarryOut, VCC, VSS
  assign Dout_2 = Enable ? Dout : 16'bz;  // Controlled_Buffer controlled_buffer_1

  // Notes on the sheet:
  //   Dout_2: pull=down
endmodule

module _8bit16transciever (
  input  Dir,
  input  nOE,
  input  [7:0] HaddrIn,
  input  [7:0] DataBusIn,
  input  nOE_2,
  input  [7:0] Laddrin,
  output [7:0] HaddrOut,
  output [7:0] DataBusOut
);

  wire and_1_out, and_2_out, and_3_out, and_4_out;
  wire [7:0] controlled_buffer_1_out, controlled_buffer_2_out;

  and and_1 (and_1_out, Dir, ~nOE);  // AND_Gate
  and and_2 (and_2_out, 1'b1, ~nOE_2);  // AND_Gate
  and and_3 (and_3_out, ~Dir, ~nOE);  // AND_Gate
  assign controlled_buffer_1_out = and_1_out ? controlled_buffer_2_out : 8'bz;  // Controlled_Buffer controlled_buffer_1
  assign controlled_buffer_2_out = and_3_out ? controlled_buffer_1_out : 8'bz;  // Controlled_Buffer controlled_buffer_2
  and and_4 (and_4_out, ~1'b1, ~nOE_2);  // AND_Gate
  assign DataBusIn = and_2_out ? Laddrin : 8'bz;  // Controlled_Buffer controlled_buffer_3
  assign Laddrin = and_4_out ? DataBusIn : 8'bz;  // Controlled_Buffer controlled_buffer_4

  assign DataBusOut = DataBusIn;
  assign HaddrOut = HaddrIn;
endmodule

module HM62256sel (
  input  nWE,
  input  nCE,
  input  nOE,
  output Sel,
  output Load
);

  wire nor_1_out;

  nor nor_1 (nor_1_out, nWE, nCE);
  nor nor_2 (Load, nCE, nOE);
  or or_1 (Sel, nor_1_out, Load);

  // Notes on the sheet:
  //   !WE
  //   !CE
  //   !OE
endmodule
